# Fritzing sketch uggh (saved by Fritzing 0.9.5d)
breadboards: 1

parts:
  Part1 = Arduino Pro Mini (5V)
  M1 = RioRand LM2596
  BAT1 = BC9VPC [package=bc9vpc]
  RS1 = RS232 Shield
  R1 = Resistor [tolerance=±5% resistance=10k package=THT]
  S1 = Toggle Switch spst [package=THT]
  JP1 = Header 2 [package=jst-2-pth-kit]

nets:
  N1: Part1.TXO, RS1.TXD
  N2: Part1.RXI, RS1.RXD
  VCC: Part1.VCC, M1.Pin_3, RS1.VCC
  GND: Part1.GND, M1.Pin_2, M1.Pin_4, BAT1.V-, RS1.GND, R1.Pin_1, JP1.2
  N3: Part1.D8, R1.Pin_0, JP1.1
  N4: M1.Pin_1, S1.COM
  N5: BAT1.V+, S1.L1

custom parts:
  RS232 Shield: RS232 connector, 4-pin, right-angle female. Designed by Dr Kristofer Chan, King's College London / remote-research.org. Licensed under Creative Commons Attribution-ShareAlike 4.0
  Toggle Switch spst: Toggle Switch single pole single throw
